// Logisim project FINAL.circ as structural Verilog: 4 circuits, main circuit main
module main (
  input  [7:0] in_1
);

  wire button_1_out, button_2_out, button_3_out, button_4_out, clock_1_out, cpu_1_gpio_0, cpu_1_gpio_1,
       cpu_1_gpio_2, cpu_1_gpio_3, cpu_1_oe, cpu_1_we;
  wire [3:0] rom_1_data;
  wire [15:0] cpu_1_code_address, cpu_1_ram_address, cpu_1_ram_in, ram_1_dout;

  ROM #(.addrWidth(16), .dataWidth(4)) rom_1 (.addr(cpu_1_code_address), .data(rom_1_data));
  Clock clock_1 (.out(clock_1_out));
  LED led_1 (.in(cpu_1_gpio_0));
  LED led_2 (.in(cpu_1_gpio_1));
  LED led_3 (.in(cpu_1_gpio_2));
  LED led_4 (.in(cpu_1_gpio_3));
  Button button_1 (.out(button_1_out));
  CPU cpu_1 (
    .pre_scl(in_1), .GPIO_6(button_3_out), .GPIO_7(button_4_out), .GPIO_4(button_1_out),
    .RAM_out(ram_1_dout), .GPIO_5(button_2_out), .code(rom_1_data), .clc(clock_1_out), .GPIO_0(cpu_1_gpio_0),
    .GPIO_1(cpu_1_gpio_1), .GPIO_2(cpu_1_gpio_2), .GPIO_3(cpu_1_gpio_3), .RAM_address(cpu_1_ram_address),
    .RAM_in(cpu_1_ram_in), .WE(cpu_1_we), .OE(cpu_1_oe), .code_address(cpu_1_code_address));
  Button button_2 (.out(button_2_out));
  Button button_3 (.out(button_3_out));
  Button button_4 (.out(button_4_out));
  RAM #(.addrWidth(16), .dataWidth(16), .trigger("high")) ram_1 (
    .addr(cpu_1_ram_address), .we(cpu_1_we), .oe(cpu_1_oe), .din(cpu_1_ram_in), .dout(ram_1_dout));

  // Notes on the sheet:
  //   contents of rom_1 (hex, n*v repeats v):
  //   d 0 7 0 d 0 7 2 d 0 8 b d 7 8 d d 1 4 e 3 d e e d 0 5 f d 0 1 d 1 e f 0 c 2
endmodule

module timer (
  input  [7:0] OCA,
  input  setOCA,
  input  [7:0] OCB,
  input  setOCB,
  input  OIE,
  input  WGM,
  input  [7:0] prescaler,
  input  clc,
  output [7:0] CNT,
  output interupt,
  output Waveform,
  output [2:0] status,
  output scaled_clc
);

  wire and_1_out, and_2_out, and_3_out, comparator_1_eq, comparator_2_eq, comparator_3_eq, comparator_4_eq,
       counter_1_carry, counter_3_carry, counter_4_carry, counter_5_carry, IFO, IFOCA, IFOCB, OCAIE, OCBIE,
       OIE_t, or_1_out, or_2_out, OWF, t_ff_1_q, WGM_t;
  wire [7:0] register_1_q, register_2_q;

  Register register_1 (.D(OCA), .clk(setOCA), .Q(register_1_q));  // open: en, clr
  Register register_2 (.D(OCB), .clk(setOCB), .Q(register_2_q));  // open: en, clr
  Register #(.width(1)) register_3 (.D(setOCA), .clk(setOCA), .Q(OCAIE));  // open: en, clr
  Register #(.width(1)) register_4 (.D(setOCB), .clk(setOCB), .Q(OCBIE));  // open: en, clr
  Register #(.width(1)) register_5 (.D(OIE), .Q(OIE_t));  // open: en, clk, clr
  Register #(.width(1)) register_6 (.D(WGM), .Q(WGM_t));  // open: en, clk, clr
  Comparator comparator_1 (.a(prescaler), .b({8{1'b0}}), .eq(comparator_1_eq));  // open: gt, lt
  Comparator comparator_2 (.a(prescaler), .b(8'h1), .eq(comparator_2_eq));  // open: gt, lt
  Counter counter_1 (
    .load(counter_1_carry), .D(prescaler), .count(clc), .carry(counter_1_carry), .up(1'b0), .clk(clc));  // open: Q, clr
  or or_1 (or_1_out, comparator_1_eq, comparator_2_eq);
  Comparator comparator_3 (.a(register_1_q), .b(CNT), .eq(comparator_3_eq));  // open: gt, lt
  Comparator comparator_4 (.a(CNT), .b(register_2_q), .eq(comparator_4_eq));  // open: gt, lt
  Multiplexer multiplexer_1 (.in0(counter_1_carry), .in1(clc), .out(scaled_clc), .sel(or_1_out));
  and and_1 (and_1_out, OCAIE, comparator_3_eq);
  and and_2 (and_2_out, comparator_4_eq, OCBIE);
  and and_3 (and_3_out, OWF, OIE_t);
  Counter counter_2 (.count(scaled_clc), .Q(CNT), .carry(OWF), .clk(scaled_clc), .clr(OWF));  // open: load, D, up
  D_Flip_Flop d_ff_1 (.D(1'b1), .clk(and_1_out), .Q(IFOCA), .reset(counter_3_carry));  // open: Qn, preset
  D_Flip_Flop d_ff_2 (.D(1'b1), .clk(and_2_out), .Q(IFOCB), .reset(counter_4_carry));  // open: Qn, preset
  D_Flip_Flop d_ff_3 (.D(1'b1), .clk(and_3_out), .Q(IFO), .reset(counter_5_carry));  // open: Qn, preset
  Counter #(.max('h2), .width(2)) counter_3 (
    .count(IFOCA), .carry(counter_3_carry), .clk(clc), .clr(counter_3_carry));  // open: load, D, Q, up
  Counter #(.max('h2), .width(2)) counter_4 (
    .count(IFOCB), .carry(counter_4_carry), .clk(clc), .clr(counter_4_carry));  // open: load, D, Q, up
  Counter #(.max('h2), .width(2)) counter_5 (
    .count(IFO), .carry(counter_5_carry), .clk(clc), .clr(counter_5_carry));  // open: load, D, Q, up
  T_Flip_Flop t_ff_1 (.T(1'b1), .clk(or_2_out), .Q(t_ff_1_q));  // open: Qn, reset, preset
  or or_2 (or_2_out, IFOCA, IFOCB);
  or or_3 (interupt, IFOCA, IFOCB, IFO);
  Register #(.width(3)) register_7 (.D({IFO, IFOCB, IFOCA}), .clk(clc), .Q(status));  // open: en, clr
  and and_4 (Waveform, t_ff_1_q, WGM_t);

  // Other names for the same wires on the sheet: clock = clc; ps[7:0] = prescaler
endmodule

module ALU (
  input  [15:0] A,
  input  [15:0] B,
  input  [3:0] control,
  output [15:0] out_4
);

  wire [3:0] bit_extender_1_out, bit_extender_2_out;
  wire [15:0] adder_1_out, and_1_out, divider_1_out, multiplier_1_out, not_1_out, or_1_out, shifter_1_out,
       shifter_2_out, subtractor_1_out, xor_1_out;

  Bit_Extender #(.in_width(16), .out_width(4)) bit_extender_1 (.in(B), .out(bit_extender_1_out));
  Bit_Extender #(.in_width(16), .out_width(4)) bit_extender_2 (.in(B), .out(bit_extender_2_out));
  Adder #(.width(16)) adder_1 (.a(A), .b(B), .out(adder_1_out));  // open: cin, cout
  Subtractor #(.width(16)) subtractor_1 (.a(A), .b(B), .out(subtractor_1_out));  // open: bin, bout
  Multiplier #(.width(16)) multiplier_1 (.a(A), .b(B), .out(multiplier_1_out));  // open: cin, cout
  Shifter #(.shift("lr"), .width(16)) shifter_1 (.in(A), .\dist (bit_extender_1_out), .out(shifter_1_out));
  Divider #(.width(16)) divider_1 (.a(A), .b(B), .out(divider_1_out));  // open: upper, rem
  Shifter #(.width(16)) shifter_2 (.in(A), .\dist (bit_extender_2_out), .out(shifter_2_out));
  assign not_1_out = ~A;  // NOT_Gate not_1, 16 bits wide
  assign and_1_out = A & B;  // AND_Gate and_1, 16 bits wide
  assign or_1_out = A | B;  // OR_Gate or_1, 16 bits wide
  assign xor_1_out = A ^ B;  // XOR_Gate xor_1, 16 bits wide
  Multiplexer #(.select(4), .width(16)) multiplexer_1 (
    .in2(adder_1_out), .in3(subtractor_1_out), .in4(multiplier_1_out), .in5(shifter_1_out),
    .in6(divider_1_out), .in7(shifter_2_out), .in8(not_1_out), .in9(and_1_out), .in10(or_1_out),
    .in11(xor_1_out), .out(out_4), .sel(control));  // open: in0, in1, in12, in13, in14, in15
endmodule

module CPU (
  input  [7:0] pre_scl,
  input  clc,
  input  [3:0] code,
  input  GPIO_4,
  input  GPIO_5,
  input  GPIO_6,
  input  GPIO_7,
  input  [15:0] RAM_out,
  output [15:0] code_address,
  output [15:0] RAM_address,
  output WE,
  output OE,
  output [15:0] RAM_in,
  output GPIO_0,
  output GPIO_1,
  output GPIO_2,
  output GPIO_3
);

  wire ALC, and_1_out, and_2_out, and_3_out, clc_t, comparator_1_lt, comparator_2_lt, comparator_3_lt,
       comparator_4_lt, comparator_5_lt, comparator_6_lt, comparator_7_eq, comparator_8_eq, D0_clc, D1_clc,
       D2_clc, D3_clc, D4_clc, D5_clc, D6_clc, D7_clc, D8_clc, D9_clc, D10_clc, D11_clc, D12_clc, D13_clc,
       D14_clc, D15_clc, demultiplexer_2_out0, demultiplexer_2_out1, demultiplexer_2_out2,
       demultiplexer_2_out3, demultiplexer_6_out3, demultiplexer_6_out5, demultiplexer_6_out6, interupt, JC,
       LC, not_1_out, not_2_out, not_3_out, or_1_out, return_0;
  wire [1:0] counter_2_q;
  wire [2:0] bitadder_1_out, timer_1_status;
  wire [3:0] control, p1_t, p2_t, p3_t;
  wire [7:0] bit_extender_1_out, bit_extender_2_out, timer_1_cnt;
  wire [15:0] ALU_A, ALU_B, ALU_out, BRANCH, BRANCH1, BRANCH2, BREQ1, BREQ2, BRNE1, BRNE2, D0_in, D0_out,
       D1_in, D1_out, D2_in, D2_out, D3_in, D3_out, D4_in, D4_out, D5_in, D5_out, D6_in, D6_out, D7_in,
       D7_out, D8_in, D8_out, D9_in, D9_out, D10_in, D10_out, D11_in, D11_out, D12_in, D12_out, D13_in,
       D13_out, D14_in, D14_out, D15_in, D15_out, IFO, IFOCA, IFOCB, JA, JUMP, LI, multiplier_1_cout,
       multiplier_1_out, multiplier_2_out, or_4_out, P1, P2, P3, RAM_adress1, RAM_adress2;

  not not_1 (not_1_out, JC);
  Counter #(.max('hffff), .trigger("falling"), .width(16)) counter_1 (
    .load(JC), .D(BRANCH), .count(not_1_out), .Q(code_address), .clk(clc_t));  // open: carry, up, clr
  Multiplexer #(.select(4), .width(16)) multiplexer_1 (
    .in0(D0_out), .in1(D1_out), .in2(D2_out), .in3(D3_out), .in4(D4_out), .in5(D5_out), .in6(D6_out),
    .in7(D7_out), .in8(D8_out), .in9(D9_out), .in10(D10_out), .in11(D11_out), .in12(D12_out), .in13(D13_out),
    .in14(D14_out), .in15(D15_out), .out(P1), .sel(p1_t));
  Multiplexer #(.select(4), .width(16)) multiplexer_2 (
    .in0(D0_out), .in1(D1_out), .in2(D2_out), .in3(D3_out), .in4(D4_out), .in5(D5_out), .in6(D6_out),
    .in7(D7_out), .in8(D8_out), .in9(D9_out), .in10(D10_out), .in11(D11_out), .in12(D12_out), .in13(D13_out),
    .in14(D14_out), .in15(D15_out), .out(P2), .sel(p2_t));
  Demultiplexer #(.select(4), .width(16)) demultiplexer_1 (
    .out0(D0_in), .out1(D1_in), .out2(D2_in), .out3(D3_in), .out4(D4_in), .out5(D5_in), .out6(D6_in),
    .out7(D7_in), .out8(D8_in), .out9(D9_in), .out10(D10_in), .out11(D11_in), .out12(D12_in), .out13(D13_in),
    .out14(D14_in), .out15(D15_in), .in(P3), .sel(p3_t));
  Demultiplexer #(.select(2)) demultiplexer_2 (
    .out0(demultiplexer_2_out0), .out1(demultiplexer_2_out1), .out2(demultiplexer_2_out2),
    .out3(demultiplexer_2_out3), .in(clc_t), .sel(counter_2_q));
  Counter #(.max('h3), .trigger("falling"), .width(2)) counter_2 (
    .count(1'b1), .Q(counter_2_q), .clk(clc_t), .clr(JC));  // open: load, D, carry, up
  ALU alu_1 (.A(ALU_A), .B(ALU_B), .control(control), .out_4(ALU_out));
  Register #(.trigger("falling"), .width(4)) order (
    .D(code), .clk(demultiplexer_2_out0), .Q(control));  // open: en, clr
  Register #(.trigger("falling"), .width(4)) u_p1 (.D(code), .clk(demultiplexer_2_out1), .Q(p1_t));  // open: en, clr
  Register #(.trigger("falling"), .width(4)) u_p2 (.D(code), .clk(demultiplexer_2_out2), .Q(p2_t));  // open: en, clr
  Register #(.trigger("falling"), .width(4)) u_p3 (.D(code), .clk(demultiplexer_2_out3), .Q(p3_t));  // open: en, clr
  Comparator #(.mode("unsigned"), .width(4)) comparator_1 (
    .a(4'b0000), .b(control), .lt(comparator_1_lt));  // open: gt, eq
  Comparator #(.mode("unsigned"), .width(4)) comparator_2 (
    .a(4'b0001), .b(control), .lt(comparator_2_lt));  // open: gt, eq
  Comparator #(.mode("unsigned"), .width(4)) comparator_3 (
    .a(4'b1011), .b(control), .lt(comparator_3_lt));  // open: gt, eq
  Comparator #(.mode("unsigned"), .width(4)) comparator_4 (
    .a(4'b1100), .b(control), .lt(comparator_4_lt));  // open: gt, eq
  Comparator #(.mode("unsigned"), .width(4)) comparator_5 (
    .a(4'b1101), .b(control), .lt(comparator_5_lt));  // open: gt, eq
  Comparator #(.mode("unsigned"), .width(4)) comparator_6 (
    .a(4'b1110), .b(control), .lt(comparator_6_lt));  // open: gt, eq
  Multiplier #(.width(16)) multiplier_1 (
    .a(D0_in), .b(16'h4), .out(multiplier_1_out), .cout(multiplier_1_cout));  // open: cin
  Multiplier #(.width(16)) multiplier_2 (
    .a(D1_in), .b(16'h4), .out(multiplier_2_out), .cin(multiplier_1_cout));  // open: cout
  not not_2 (not_2_out, return_0);
  or or_1 (or_1_out, OE, LC, ALC);
  Multiplexer #(.select(4), .width(16)) multiplexer_3 (
    .in0(D0_out), .in1(D1_out), .in2(D2_out), .in3(D3_out), .in4(D4_out), .in5(D5_out), .in6(D6_out),
    .in7(D7_out), .in8(D8_out), .in9(D9_out), .in10(D10_out), .in11(D11_out), .in12(D12_out), .in13(D13_out),
    .in14(D14_out), .in15(D15_out), .out(JA), .sel(p3_t));
  Bit_Extender #(.in_width(16), .out_width(8)) bit_extender_1 (.in(multiplier_1_out), .out(bit_extender_1_out));
  Bit_Extender #(.in_width(16), .out_width(8)) bit_extender_2 (.in(multiplier_2_out), .out(bit_extender_2_out));
  and and_1 (and_1_out, clc, not_2_out);
  BitAdder #(.width(1)) bitadder_1 (
    .in0(comparator_1_lt), .in1(comparator_2_lt), .in2(comparator_3_lt), .in3(comparator_4_lt),
    .in4(comparator_5_lt), .in5(comparator_6_lt), .out(bitadder_1_out));
  Demultiplexer #(.select(4)) demultiplexer_3 (
    .out0(D0_clc), .out1(D1_clc), .out2(D2_clc), .out3(D3_clc), .out4(D4_clc), .out5(D5_clc), .out6(D6_clc),
    .out7(D7_clc), .out8(D8_clc), .out9(D9_clc), .out10(D10_clc), .out11(D11_clc), .out12(D12_clc),
    .out13(D13_clc), .out14(D14_clc), .out15(D15_clc), .in(or_1_out), .sel(p3_t));
  assign LI = {{8{1'b0}}, {p1_t, p2_t}};  // Bit_Extender bit_extender_3
  Register #(.width(16)) D0 (.D(D0_in), .clk(D0_clc), .Q(D0_out));  // open: en, clr
  Register #(.width(16)) D4 (.D(D4_in), .clk(D4_clc), .Q(D4_out));  // open: en, clr
  assign D8_out = {{15{GPIO_6}}, GPIO_6};  // Bit_Extender bit_extender_4
  Register #(.width(16)) D12 (.D(D12_in), .clk(D12_clc), .Q(D12_out));  // open: en, clr
  Demultiplexer #(.select(3), .width(16)) demultiplexer_4 (
    .out0(RAM_adress2), .out1(RAM_in), .out2(ALU_A), .out3(JUMP), .out5(BRNE1), .out6(BREQ1), .in(P1),
    .sel(bitadder_1_out));  // open: out4, out7
  Demultiplexer #(.select(3), .width(16)) demultiplexer_5 (
    .out1(RAM_adress1), .out2(ALU_B), .out5(BRNE2), .out6(BREQ2), .in(P2), .sel(bitadder_1_out));  // open: out0, out3, out4, out7
  Multiplexer #(.select(3), .width(16)) multiplexer_4 (
    .in0(RAM_out), .in2(ALU_out), .in4(LI), .out(P3), .sel(bitadder_1_out));  // open: in1, in3, in5, in6, in7
  Demultiplexer #(.select(3)) demultiplexer_6 (
    .out0(OE), .out1(WE), .out2(ALC), .out3(demultiplexer_6_out3), .out4(LC), .out5(demultiplexer_6_out5),
    .out6(demultiplexer_6_out6), .in(demultiplexer_2_out0), .sel(bitadder_1_out));  // open: out7
  Demultiplexer #(.select(3), .width(16)) demultiplexer_7 (
    .out5(BRANCH1), .out6(BRANCH2), .in(JA), .sel(bitadder_1_out));  // open: out0, out1, out2, out3, out4, out7
  timer timer_1 (
    .OCA(bit_extender_1_out), .setOCA(D0_clc), .OCB(bit_extender_2_out), .setOCB(D1_clc), .OIE(D10_clc),
    .prescaler(pre_scl), .clc(and_1_out), .CNT(timer_1_cnt), .interupt(interupt), .status(timer_1_status),
    .scaled_clc(clc_t));  // open: WGM, Waveform
  Register #(.width(16)) D1 (.D(D1_in), .clk(D1_clc), .Q(D1_out));  // open: en, clr
  Register #(.width(16)) D5 (.D(D5_in), .clk(D5_clc), .Q(D5_out));  // open: en, clr
  assign D9_out = {{15{GPIO_7}}, GPIO_7};  // Bit_Extender bit_extender_5
  Register #(.width(16)) D13 (.D(D13_in), .clk(D13_clc), .Q(D13_out));  // open: en, clr
  Multiplexer #(.width(16)) multiplexer_5 (.in0({16{1'b0}}), .in1(D11_out), .out(IFOCA), .sel(timer_1_status[0]));
  Multiplexer #(.width(16)) multiplexer_6 (.in0({16{1'b0}}), .in1(D12_out), .out(IFOCB), .sel(timer_1_status[1]));
  Multiplexer #(.width(16)) multiplexer_7 (.in0({16{1'b0}}), .in1(D10_out), .out(IFO), .sel(timer_1_status[2]));
  Comparator #(.width(16)) comparator_7 (.a(BRNE1), .b(BRNE2), .eq(comparator_7_eq));  // open: gt, lt
  Comparator #(.width(16)) comparator_8 (.a(BREQ1), .b(BREQ2), .eq(comparator_8_eq));  // open: gt, lt
  not not_3 (not_3_out, comparator_7_eq);
  and and_2 (and_2_out, not_3_out, demultiplexer_6_out5);
  and and_3 (and_3_out, demultiplexer_6_out6, comparator_8_eq);
  Comparator #(.width(16)) comparator_9 (.a(D2_out), .b(16'h1), .eq(GPIO_0));  // open: gt, lt
  Comparator #(.width(16)) comparator_10 (.a(D3_out), .b(16'h1), .eq(GPIO_1));  // open: gt, lt
  Comparator #(.width(16)) comparator_11 (.a(D4_out), .b(16'h1), .eq(GPIO_2));  // open: gt, lt
  Comparator #(.width(16)) comparator_12 (.a(D5_out), .b(16'h1), .eq(GPIO_3));  // open: gt, lt
  Register #(.width(16)) D2 (.D(D2_in), .clk(D2_clc), .Q(D2_out));  // open: en, clr
  assign D6_out = {{15{GPIO_4}}, GPIO_4};  // Bit_Extender bit_extender_6
  Register #(.width(16)) D10 (.D(D10_in), .clk(D10_clc), .Q(D10_out));  // open: en, clr
  Register #(.width(16)) D14 (.D(D14_in), .clk(D14_clc), .Q(D14_out));  // open: en, clr
  assign RAM_address = RAM_adress1 | RAM_adress2;  // OR_Gate or_2, 16 bits wide
  or or_3 (JC, demultiplexer_6_out3, and_2_out, and_3_out, interupt);
  assign or_4_out = JUMP | BRANCH1 | BRANCH2 | IFOCA | IFOCB | IFO;  // OR_Gate or_4, 16 bits wide
  Register #(.width(16)) D3 (.D(D3_in), .clk(D3_clc), .Q(D3_out));  // open: en, clr
  Register #(.width(16)) D11 (.D(D11_in), .clk(D11_clc), .Q(D11_out));  // open: en, clr
  Register #(.width(16)) D15 (.D(D15_in), .clk(D15_clc), .Q(D15_out));  // open: en, clr
  Comparator #(.width(16)) comparator_13 (.a(D13_out), .b(16'h1), .eq(return_0));  // open: gt, lt
  Multiplier #(.width(16)) multiplier_3 (.a(or_4_out), .b(16'h4), .out(BRANCH));  // open: cin, cout
  assign D7_out = {{15{GPIO_5}}, GPIO_5};  // Bit_Extender bit_extender_7

  // Other names for the same wires on the sheet: LOAD = OE; STORE = WE
endmodule
